# Fritzing sketch dragonboard410c_96boardGPIO_test (saved by Fritzing 0.9.3b)
breadboards: 1

parts:
  96boards_CE1 = 96boards Consumer Edition
  S1 = Momentary Switch [package=ksa_sealed_tac_switch]
  LED1 = LED - 5mm [color="Red (633nm)" package="5 mm [THT]"]

nets:
  N1: 96boards_CE1.GND, LED1.cathode
  N2: 96boards_CE1.GPIO-A, S1.4
  N3: 96boards_CE1.GPIO-C, LED1.anode
  N4: 96boards_CE1.1V8, S1.2

custom parts:
  96boards Consumer Edition: 96boards is the first open specification to define a platform for the delivery of compatible low-cost, small footprint 32-bit and 64-bit Cortex-A boards from the range of ARM SoC vendors. Standardized expansion buses for peripheral I/O, display and cameras allow the hardware ecosystem to develop a range of compatible add-on products that will work on any 96Boards product over the lifetime of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
